# Fritzing sketch Arduino_Controller_Pin_Diagram (saved by Fritzing 0.9.3b)
breadboards: 1

parts:
  Arduino_Nano = Arduino Nano (Rev3.0)
  Keyes_2-channel_Relay = Keyes Relay [package=THT]
  KY-2 = Keyes Relay [package=THT]
  Q1 = NPN-Transistor [package="TO92 [THT]"]
  R1 = Resistor [tolerance=±5% resistance=1k package="1206 [SMD]"]
  P1_(left)_Flipper_Button = Arcade Button (blue)
  P2_(right)_Flipper_Button = Arcade Button (blue)
  12V_Power_Supply = Power plug
  Left_Flipper_Solenoid = Solenoid
  P1/P2/Coin_LEDs = LED - 5mm [color="White (8000K)" package="5 mm [THT]"]
  Left_Flipper_Solenoid1 = Solenoid
  P1/P2/Coin_LEDs1 = LED - 5mm [color="White (8000K)" package="5 mm [THT]"]
  P1/P2/Coin_LEDs2 = LED - 5mm [color="White (8000K)" package="5 mm [THT]"]
  P1/P2/Coin_LEDs3 = LED - 5mm [color="White (8000K)" package="5 mm [THT]"]

nets:
  GND: Arduino_Nano.GND, Arduino_Nano.VIN, Keyes_2-channel_Relay.power, KY-2.power, Q1.B
  N1: Arduino_Nano.D2, Keyes_2-channel_Relay.signal
  N2: Arduino_Nano.D3, KY-2.signal
  N3: Arduino_Nano.D4, R1.Pin_0
  N4: Arduino_Nano.A1, P2_(right)_Flipper_Button.no_name_yet
  N5: Arduino_Nano.A0, P1_(left)_Flipper_Button.no_name_yet
  N6: Keyes_2-channel_Relay.ground, KY-2.ground, P1/P2/Coin_LEDs.cathode, P1/P2/Coin_LEDs1.cathode, P1/P2/Coin_LEDs2.cathode, P1/P2/Coin_LEDs3.cathode
  N7: Keyes_2-channel_Relay.C, KY-2.C, 12V_Power_Supply.GND
  N8: Keyes_2-channel_Relay.NO, Left_Flipper_Solenoid.pin1
  N9: KY-2.NO, Left_Flipper_Solenoid1.pin1
  N10: Q1.E, P1/P2/Coin_LEDs.anode, P1/P2/Coin_LEDs1.anode, P1/P2/Coin_LEDs2.anode, P1/P2/Coin_LEDs3.anode
  N11: Q1.C, R1.Pin_1
  N12: 12V_Power_Supply.VCC, Left_Flipper_Solenoid.pin2, Left_Flipper_Solenoid1.pin2

custom parts:
  Keyes Relay: The Keyes 5V relay module is suitable for SCM development, home appliance control. It uses a 5V~12V TIL control signal which can control DC / AC signal.
  Arcade Button (blue): Adafruit Arcade Button (blue)
