# Fritzing sketch Wireless_Transmitter (saved by Fritzing 0.9.3b)

parts:
  Pro_Micro1 = SparkFun Pro Micro
  part = Resistor [tolerance=±5% resistance=1k package="0805 [SMD]"]
  part_2 = Resistor [tolerance=±5% resistance=22 package="0805 [SMD]"]
  Q1 = NPN-Transistor [package="TO92 [THT]"]
  NRF24L01 = NRF24L01+ Breakout Board
  470uF_10V = Capacitor Polarized [package=cpol-radial-10uf-25v]
  Middle_Pedal = D2F-FL Omron Snap Action Limit Switch with Level
  Right_Pedal = D2F-FL Omron Snap Action Limit Switch with Level
  Left_Pedal = D2F-FL Omron Snap Action Limit Switch with Level

nets:
  N1: Pro_Micro1.TX0, part.Pin_0
  GND: Pro_Micro1.GND, part_2.Pin_0, NRF24L01.GND, 470uF_10V.-
  N2: Pro_Micro1.8, Left_Pedal.COM
  N3: Pro_Micro1.9, Middle_Pedal.COM
  N4: Pro_Micro1.10, Right_Pedal.COM
  N5: Pro_Micro1.16, NRF24L01.MOSI
  N6: Pro_Micro1.14, NRF24L01.MISO
  N7: Pro_Micro1.15, NRF24L01.SCK
  N8: Pro_Micro1.A0, NRF24L01.CS
  N9: Pro_Micro1.A1, NRF24L01.CE
  N10: Pro_Micro1.VCC, Q1.C
  N11: NRF24L01.VCC, 470uF_10V.+
  N12: Middle_Pedal.NO, Right_Pedal.NO

custom parts:
  SparkFun Pro Micro: The Pro Micro is similar to the Pro Mini except with an ATmega32U4 on board. The USB transceiver inside the 32U4 allows us to add USB connectivity on-board and do away with bulky external USB interface. Based on: https://github.com/unorthodox-engineers/unorthodox-arduino/blob/master/Unorthodox/fritzing/parts/Pro%20Micro.fzpz
  D2F-FL Omron Snap Action Limit Switch with Level: Snap action switch with stainless steel lever.
